// Logisim project td4_cpu.circ as structural Verilog: 3 circuits, main circuit main
module main (
  input  clear,
  input  CK,
  input  input_port_0,
  input  input_port_1,
  input  input_port_2,
  input  input_port_3
);

  wire clock_1_out, custom_74hc283_1_c4, d_ff_1_q, multiplexer_1_out, multiplexer_2_out, multiplexer_3_out,
       multiplexer_4_out, nand_1_out, nand_2_out, not_1_out, not_2_out, not_3_out, not_4_out, not_5_out,
       not_6_out, or_1_out, or_2_out, or_4_out, or_5_out;
  wire [0:0] or_3_out;
  wire [3:0] counter_1_q, counter_2_q, counter_3_q, counter_4_q, custom_74hc283_1_s1;
  wire [7:0] rom_1_data;

  Clock clock_1 (.out(clock_1_out));
  or or_1 (or_1_out, CK, clock_1_out);
  not not_1 (not_1_out, or_4_out);
  not not_2 (not_2_out, or_5_out);
  not not_3 (not_3_out, nand_1_out);
  not not_4 (not_4_out, nand_2_out);
  Counter #(.max('hf), .width(4)) counter_1 (
    .clr(clear), .load(not_1_out), .up(1'b1), .count(1'b0), .clk(or_1_out), .D(custom_74hc283_1_s1),
    .Q(counter_1_q));  // open: carry
  Counter #(.max('hf), .width(4)) counter_2 (
    .clr(clear), .load(not_2_out), .up(1'b1), .count(1'b0), .clk(or_1_out), .D(custom_74hc283_1_s1),
    .Q(counter_2_q));  // open: carry
  Counter #(.max('hf), .width(4)) counter_3 (
    .clr(clear), .load(not_3_out), .up(1'b1), .count(1'b0), .clk(or_1_out), .D(custom_74hc283_1_s1),
    .Q(counter_3_q));  // open: carry
  Counter #(.max('hf), .width(4)) counter_4 (
    .clr(clear), .load(not_4_out), .up(1'b1), .count(1'b1), .clk(or_1_out), .D(custom_74hc283_1_s1),
    .Q(counter_4_q));  // open: carry
  Multiplexer #(.select(2)) multiplexer_1 (
    .in0(counter_1_q[0]), .in1(counter_2_q[0]), .in2(input_port_0), .in3(1'b0), .out(multiplexer_1_out),
    .sel({rom_1_data[5], or_3_out[0]}));
  Multiplexer #(.select(2)) multiplexer_2 (
    .in0(counter_1_q[1]), .in1(counter_2_q[1]), .in2(input_port_1), .in3(1'b0), .out(multiplexer_2_out),
    .sel({rom_1_data[5], or_3_out[0]}));
  Multiplexer #(.select(2)) multiplexer_3 (
    .in0(counter_1_q[2]), .in1(counter_2_q[2]), .in2(input_port_2), .in3(1'b0), .out(multiplexer_3_out),
    .sel({rom_1_data[5], or_3_out[0]}));
  Multiplexer #(.select(2)) multiplexer_4 (
    .in0(counter_1_q[3]), .in1(counter_2_q[3]), .in2(input_port_3), .in3(1'b0), .out(multiplexer_4_out),
    .sel({2{or_3_out[0]}}));
  ROM #(.addrWidth(4)) rom_1 (.addr(counter_4_q), .data(rom_1_data));
  LED LED_0 (.in(counter_3_q[0]));
  LED LED_1 (.in(counter_3_q[1]));
  LED LED_2 (.in(counter_3_q[2]));
  LED LED_3 (.in(counter_3_q[3]));
  custom_74HC283 custom_74hc283_1 (
    .A1(multiplexer_1_out), .B1(rom_1_data[0]), .A2(multiplexer_2_out), .B2(rom_1_data[1]),
    .A3(multiplexer_3_out), .B3(rom_1_data[2]), .A4(multiplexer_4_out), .B4(rom_1_data[3]),
    .S1(custom_74hc283_1_s1[0]), .S2(custom_74hc283_1_s1[1]), .S3(custom_74hc283_1_s1[2]),
    .S4(custom_74hc283_1_s1[3]), .C4(custom_74hc283_1_c4));
  not not_5 (not_5_out, d_ff_1_q);
  D_Flip_Flop d_ff_1 (.D(custom_74hc283_1_c4), .clk(or_1_out), .Q(d_ff_1_q));  // open: Qn, preset, reset
  not not_6 (not_6_out, rom_1_data[6]);
  or or_2 (or_2_out, rom_1_data[4], not_5_out);
  or or_3 (or_3_out[0], rom_1_data[4], rom_1_data[7]);
  or or_4 (or_4_out, rom_1_data[6], rom_1_data[7]);
  or or_5 (or_5_out, not_6_out, rom_1_data[7]);
  nand nand_1 (nand_1_out, not_6_out, rom_1_data[7]);
  nand nand_2 (nand_2_out, rom_1_data[7], rom_1_data[6], or_2_out);

  // Notes on the sheet:
  //   contents of rom_1 (hex, n*v repeats v):
  //   b7 1 e1 1 e3 b6 1 e6 1 e8 b0 b4 1 ea b8 ff
endmodule

module custom_74HC161 (
  input  A,
  input  B,
  input  C,
  input  D,
  input  LD,
  input  CK,
  output QA,
  output QB,
  output QC,
  output QD
);

  wire d_ff_1_qn, multiplexer_1_out, multiplexer_2_out, multiplexer_3_out, multiplexer_4_out, not_1_out;

  Multiplexer multiplexer_1 (.in0(QA), .in1(A), .out(multiplexer_1_out), .sel(not_1_out));
  Multiplexer multiplexer_2 (.in0(QB), .in1(B), .out(multiplexer_2_out), .sel(not_1_out));
  Multiplexer multiplexer_3 (.in0(QC), .in1(C), .out(multiplexer_3_out), .sel(not_1_out));
  Multiplexer multiplexer_4 (.in0(QD), .in1(D), .out(multiplexer_4_out), .sel(not_1_out));
  not not_1 (not_1_out, LD);
  D_Flip_Flop d_ff_1 (.D(multiplexer_1_out), .clk(CK), .Q(QA), .Qn(d_ff_1_qn));  // open: preset, reset
  D_Flip_Flop d_ff_2 (.D(multiplexer_2_out), .clk(CK), .Q(QB));  // open: Qn, preset, reset
  D_Flip_Flop d_ff_3 (.D(multiplexer_3_out), .clk(CK), .Q(QC));  // open: Qn, preset, reset
  D_Flip_Flop d_ff_4 (.D(multiplexer_4_out), .clk(CK), .Q(QD));  // open: Qn, preset, reset
endmodule

module custom_74HC283 (
  input  A1,
  input  B1,
  input  A2,
  input  B2,
  input  A3,
  input  B3,
  input  A4,
  input  B4,
  output S1,
  output S2,
  output S3,
  output S4,
  output C4
);

  wire adder_1_cout, adder_2_cout, adder_3_cout;

  Adder #(.width(1)) adder_1 (.a(A1), .b(B1), .out(S1), .cout(adder_1_cout));  // open: cin
  Adder #(.width(1)) adder_2 (.a(A2), .b(B2), .out(S2), .cin(adder_1_cout), .cout(adder_2_cout));
  Adder #(.width(1)) adder_3 (.a(A3), .b(B3), .out(S3), .cin(adder_2_cout), .cout(adder_3_cout));
  Adder #(.width(1)) adder_4 (.a(A4), .b(B4), .out(S4), .cin(adder_3_cout), .cout(C4));
endmodule
