// Logisim project temp.circ as structural Verilog: 1 circuit, main circuit main
module main (
  input  in_1,
  input  C0,
  input  C1,
  input  C2,
  input  C3,
  input  A,
  input  in_7,
  input  B,
  input  in_9,
  input  in_10,
  input  in_11,
  input  in_12,
  input  in_13,
  input  in_14,
  input  in_15,
  input  in_16,
  input  in_17,
  input  in_18,
  input  in_19,
  input  in_20,
  input  in_21,
  input  in_22,
  input  in_23,
  input  in_24,
  input  in_25,
  input  in_26,
  output out_27,
  output out_28,
  output out_29,
  output out_30,
  output out_31,
  output out_32,
  output out_33,
  output out_34,
  output out_35,
  output out_36,
  output out_37
);

  wire and_1_out, and_2_out, and_3_out, and_5_out, d_ff_1_q, d_ff_2_q, multiplexer_1_out, not_1_out,
       not_2_out, not_3_out, xor_2_out;

  not not_1 (not_1_out, d_ff_1_q);
  D_Flip_Flop d_ff_1 (.D(not_1_out), .clk(in_1), .Q(d_ff_1_q));  // open: Qn, preset, reset
  D_Flip_Flop d_ff_2 (.D(multiplexer_1_out), .clk(in_7), .Q(d_ff_2_q));  // open: Qn, preset, reset
  not not_2 (not_2_out, in_12);
  not not_3 (not_3_out, d_ff_2_q);
  and and_1 (and_1_out, in_10, in_12);
  and and_2 (and_2_out, in_11, not_2_out);
  and and_3 (and_3_out, in_16, in_17);
  Counter #(.max('hf), .width(4)) counter_1 (
    .clr(in_18), .load(in_19), .up(in_20), .count(in_21), .clk(in_22), .D({in_26, in_25, in_24, in_23}),
    .carry(out_33), .Q({out_37, out_36, out_35, out_34}));
  Multiplexer multiplexer_1 (.in0(d_ff_2_q), .in1(not_3_out), .out(multiplexer_1_out), .sel(in_9));
  or or_1 (out_28, and_1_out, and_2_out);
  xor xor_1 (out_29, in_13, in_14);
  and and_4 (out_30, in_13, in_14);
  xor xor_2 (xor_2_out, in_16, in_17);
  xor xor_3 (out_31, in_15, xor_2_out);
  and and_5 (and_5_out, in_15, xor_2_out);
  or or_2 (out_32, and_5_out, and_3_out);
  Multiplexer #(.select(2)) multiplexer_2 (.in0(C0), .in1(C1), .in2(C2), .in3(C3), .out(out_27), .sel({B, A}));
endmodule
